# Fritzing sketch 2 LED (saved by Fritzing 0.9.3b)
breadboards: 1

parts:
  Part1 = Arduino Mega 2560 (Rev3)
  LED1 = LED - 5mm [color="Red (633nm)" package="5 mm [THT]"]
  LED2 = LED - 5mm [color="Red (633nm)" package="5 mm [THT]"]

nets:
  N1: Part1.D10_PWM, LED2.anode
  N2: Part1.D8_PWM, LED1.anode
  N3: Part1.GND, LED1.cathode, LED2.cathode
