# Fritzing sketch LED_and_POT (saved by Fritzing 0.9.3b)
breadboards: 1

parts:
  Part1 = Arduino Mega 2560 (Rev3)
  LED1 = LED - 5mm [color="Red (633nm)" package="5 mm [THT]"]
  R1 = Rotary Potentiometer (Small) [maximum_resistance=100kΩ package=THT]

nets:
  N1: Part1.A7, R1.wiper
  N2: Part1.D8_PWM, LED1.anode
  N3: Part1.5V, R1.leg2
  N4: Part1.GND, LED1.cathode, R1.leg1
